// Logisim project ConversorParaleloSerial.circ as structural Verilog
module main (
  input  Ap,
  input  Bp,
  input  Cp,
  input  Dp,
  input  S1,
  input  S2,
  input  DSL,
  input  DSR,
  input  CLOCK,
  input  RESET,
  output Qa,
  output Qb,
  output Qc,
  output Qd
);

  wire and_1_out, and_2_out, and_3_out, and_4_out, and_5_out, and_6_out, and_7_out, and_8_out, and_9_out,
       and_10_out, and_11_out, and_12_out, and_13_out, and_14_out, and_15_out, and_16_out, not_1_out,
       not_2_out, not_3_out, or_1_out, or_2_out, or_3_out, or_4_out;

  not not_1 (not_1_out, S1);
  not not_2 (not_2_out, S2);
  and and_1 (and_1_out, DSR, not_1_out, S2);
  and and_2 (and_2_out, S2, S1, Ap);
  not not_3 (not_3_out, RESET);
  and and_3 (and_3_out, not_2_out, S1, Qb);
  or or_1 (or_1_out, and_1_out, and_2_out, and_3_out, and_4_out);
  and and_4 (and_4_out, not_2_out, not_1_out, Qa);
  D_Flip_Flop d_ff_1 (.D(or_1_out), .clk(CLOCK), .Q(Qa), .reset(not_3_out));  // open: Qn, preset
  and and_5 (and_5_out, Qa, not_1_out, S2);
  and and_6 (and_6_out, S2, S1, Bp);
  or or_2 (or_2_out, and_5_out, and_6_out, and_7_out, and_8_out);
  and and_7 (and_7_out, not_2_out, S1, Qc);
  and and_8 (and_8_out, not_2_out, not_1_out, Qb);
  D_Flip_Flop d_ff_2 (.D(or_2_out), .clk(CLOCK), .Q(Qb), .reset(not_3_out));  // open: Qn, preset
  and and_9 (and_9_out, Qb, not_1_out, S2);
  and and_10 (and_10_out, S2, S1, Cp);
  and and_11 (and_11_out, not_2_out, S1, Qd);
  or or_3 (or_3_out, and_9_out, and_10_out, and_11_out, and_12_out);
  and and_12 (and_12_out, not_2_out, not_1_out, Qc);
  D_Flip_Flop d_ff_3 (.D(or_3_out), .clk(CLOCK), .Q(Qc), .reset(not_3_out));  // open: Qn, preset
  and and_13 (and_13_out, Qc, not_1_out, S2);
  and and_14 (and_14_out, S2, S1, Dp);
  or or_4 (or_4_out, and_13_out, and_14_out, and_15_out, and_16_out);
  and and_15 (and_15_out, not_2_out, S1, DSL);
  and and_16 (and_16_out, not_2_out, not_1_out, Qd);
  D_Flip_Flop d_ff_4 (.D(or_4_out), .clk(CLOCK), .Q(Qd), .reset(not_3_out));  // open: Qn, preset
endmodule

module Circuito4Bits (
  input  RESET
);

  wire bcd_7seg_1_sa, bcd_7seg_1_sb, bcd_7seg_1_sc, bcd_7seg_1_sd, bcd_7seg_1_se, bcd_7seg_1_sf,
       bcd_7seg_1_sg, bcd_7seg_2_sa, bcd_7seg_2_sb, bcd_7seg_2_sc, bcd_7seg_2_sd, bcd_7seg_2_se,
       bcd_7seg_2_sf, bcd_7seg_2_sg, CLOCK_out, dipswitch_1_p1, dipswitch_1_p2, dipswitch_1_p3,
       dipswitch_1_p4, LOAD_out, main_1_qa, main_1_qb, main_1_qc, main_1_qd, main_2_qa, main_2_qb, main_2_qc,
       main_2_qd, nor_1_out;

  Button CLOCK (.out(CLOCK_out));
  Button LOAD (.out(LOAD_out));
  // DipSwitch #(.number(4)) dipswitch_1: pin names not known; wires that end beside it: dipswitch_1_p1, dipswitch_1_p2, dipswitch_1_p3, dipswitch_1_p4
  nor nor_1 (nor_1_out, LOAD_out, CLOCK_out);
  main main_1 (
    .Ap(dipswitch_1_p1), .Bp(dipswitch_1_p2), .Cp(dipswitch_1_p3), .Dp(dipswitch_1_p4), .S1(LOAD_out),
    .S2(1'b1), .DSL(1'b0), .CLOCK(nor_1_out), .RESET(RESET), .Qa(main_1_qa), .Qb(main_1_qb), .Qc(main_1_qc),
    .Qd(main_1_qd));  // open: DSR
  bcd_7seg bcd_7seg_1 (
    .A(dipswitch_1_p1), .B(dipswitch_1_p2), .C(dipswitch_1_p3), .D(dipswitch_1_p4), .sb(bcd_7seg_1_sb),
    .sa(bcd_7seg_1_sa), .sf(bcd_7seg_1_sf), .sg(bcd_7seg_1_sg), .se(bcd_7seg_1_se), .sd(bcd_7seg_1_sd),
    .sc(bcd_7seg_1_sc));
  _7_Segment_Display u_7_segment_display_1 (
    .g(bcd_7seg_1_sg), .f(bcd_7seg_1_sf), .a(bcd_7seg_1_sa), .b(bcd_7seg_1_sb), .e(bcd_7seg_1_se),
    .d(bcd_7seg_1_sd), .c(bcd_7seg_1_sc));  // open: dp
  LED LEDR0 (.in(main_1_qd));
  main main_2 (
    .S1(1'b0), .S2(1'b1), .DSL(1'b0), .DSR(main_1_qd), .CLOCK(CLOCK_out), .RESET(RESET), .Qa(main_2_qa),
    .Qb(main_2_qb), .Qc(main_2_qc), .Qd(main_2_qd));  // open: Ap, Bp, Cp, Dp
  bcd_7seg bcd_7seg_2 (
    .A(main_2_qa), .B(main_2_qb), .C(main_2_qc), .D(main_2_qd), .sb(bcd_7seg_2_sb), .sa(bcd_7seg_2_sa),
    .sf(bcd_7seg_2_sf), .sg(bcd_7seg_2_sg), .se(bcd_7seg_2_se), .sd(bcd_7seg_2_sd), .sc(bcd_7seg_2_sc));
  _7_Segment_Display u_7_segment_display_2 (
    .g(bcd_7seg_2_sg), .f(bcd_7seg_2_sf), .a(bcd_7seg_2_sa), .b(bcd_7seg_2_sb), .e(bcd_7seg_2_se),
    .d(bcd_7seg_2_sd), .c(bcd_7seg_2_sc));  // open: dp
endmodule

module BCD99 (
  input  A,
  input  B,
  input  C,
  input  D,
  input  E,
  input  F,
  input  G,
  input  H,
  output B1,
  output A1,
  output F1,
  output G1,
  output E1,
  output D1,
  output C1,
  output B2,
  output A2,
  output F2,
  output G2,
  output E2,
  output D2,
  output C2
);

  bcd_7seg bcd_7seg_1 (.A(A), .B(B), .C(C), .D(D), .sb(B1), .sa(A1), .sf(F1), .sg(G1), .se(E1), .sd(D1), .sc(C1));
  bcd_7seg bcd_7seg_2 (.A(E), .B(F), .C(G), .D(H), .sb(B2), .sa(A2), .sf(F2), .sg(G2), .se(E2), .sd(D2), .sc(C2));
endmodule

module RL8 (
  input  in_1
);

  wire and_1_out, bcd99_1_a1, bcd99_1_a2, bcd99_1_b1, bcd99_1_b2, bcd99_1_c1, bcd99_1_c2, bcd99_1_d1,
       bcd99_1_d2, bcd99_1_e1, bcd99_1_e2, bcd99_1_f1, bcd99_1_f2, bcd99_1_g1, bcd99_1_g2, bcd99_2_a1,
       bcd99_2_a2, bcd99_2_b1, bcd99_2_b2, bcd99_2_c1, bcd99_2_c2, bcd99_2_d1, bcd99_2_d2, bcd99_2_e1,
       bcd99_2_e2, bcd99_2_f1, bcd99_2_f2, bcd99_2_g1, bcd99_2_g2, button_1_out, CLOCK, dipswitch_1_p1,
       dipswitch_1_p2, dipswitch_1_p3, dipswitch_1_p4, dipswitch_1_p5, dipswitch_1_p6, dipswitch_1_p7,
       dipswitch_1_p8, even_parity_2_out, not_1_out, or_1_out, PARIDADE, shift_register_1_p14,
       shift_register_2_p4, shift_register_2_p5, shift_register_2_p6, shift_register_2_p7,
       shift_register_2_p8, shift_register_2_p9, shift_register_2_p10, shift_register_2_p11,
       shift_register_2_p12;

  // DipSwitch dipswitch_1: pin names not known; wires that end beside it: dipswitch_1_p1, dipswitch_1_p2, dipswitch_1_p3, dipswitch_1_p4, dipswitch_1_p5, dipswitch_1_p6, dipswitch_1_p7, dipswitch_1_p8
  Button button_1 (.out(button_1_out));
  Button button_2 (.out(CLOCK));
  not not_1 (not_1_out, button_1_out);
  or or_1 (or_1_out, button_1_out, CLOCK);
  xnor even_parity_1 (PARIDADE, dipswitch_1_p1, dipswitch_1_p2, dipswitch_1_p3, dipswitch_1_p4, dipswitch_1_p5, dipswitch_1_p6, dipswitch_1_p7, dipswitch_1_p8);
  // Shift_Register #(.length(9)) shift_register_1: pin names not known; wires that end beside it: in_1, button_1_out, not_1_out, or_1_out, dipswitch_1_p1, dipswitch_1_p2, dipswitch_1_p3, dipswitch_1_p4, dipswitch_1_p5, dipswitch_1_p6, dipswitch_1_p7, dipswitch_1_p8, PARIDADE, shift_register_1_p14
  LED led_1 (.in(PARIDADE));
  BCD99 bcd99_1 (
    .A(dipswitch_1_p1), .B(dipswitch_1_p2), .C(dipswitch_1_p3), .D(dipswitch_1_p4), .E(dipswitch_1_p5),
    .F(dipswitch_1_p6), .G(dipswitch_1_p7), .H(dipswitch_1_p8), .B1(bcd99_1_b1), .A1(bcd99_1_a1),
    .F1(bcd99_1_f1), .G1(bcd99_1_g1), .E1(bcd99_1_e1), .D1(bcd99_1_d1), .C1(bcd99_1_c1), .B2(bcd99_1_b2),
    .A2(bcd99_1_a2), .F2(bcd99_1_f2), .G2(bcd99_1_g2), .E2(bcd99_1_e2), .D2(bcd99_1_d2), .C2(bcd99_1_c2));
  LED led_2 (.in(shift_register_1_p14));
  _7_Segment_Display u_7_segment_display_1 (
    .g(bcd99_1_g1), .f(bcd99_1_f1), .a(bcd99_1_a1), .b(bcd99_1_b1), .e(bcd99_1_e1), .d(bcd99_1_d1),
    .c(bcd99_1_c1));  // open: dp
  // Shift_Register #(.length(9)) shift_register_2: pin names not known; wires that end beside it: in_1, CLOCK, shift_register_1_p14, shift_register_2_p4, shift_register_2_p5, shift_register_2_p6, shift_register_2_p7, shift_register_2_p8, shift_register_2_p9, shift_register_2_p10, shift_register_2_p11, shift_register_2_p12
  _7_Segment_Display u_7_segment_display_2 (
    .g(bcd99_1_g2), .f(bcd99_1_f2), .a(bcd99_1_a2), .b(bcd99_1_b2), .e(bcd99_1_e2), .d(bcd99_1_d2),
    .c(bcd99_1_c2));  // open: dp
  xnor even_parity_2 (even_parity_2_out, shift_register_2_p4, shift_register_2_p5, shift_register_2_p6, shift_register_2_p7, shift_register_2_p8, shift_register_2_p9, shift_register_2_p10, shift_register_2_p11);
  LED led_3 (.in(shift_register_2_p12));
  LED led_4 (.in(even_parity_2_out));
  BCD99 bcd99_2 (
    .A(shift_register_2_p4), .B(shift_register_2_p5), .C(shift_register_2_p6), .D(shift_register_2_p7),
    .E(shift_register_2_p8), .F(shift_register_2_p9), .G(shift_register_2_p10), .H(shift_register_2_p11),
    .B1(bcd99_2_b1), .A1(bcd99_2_a1), .F1(bcd99_2_f1), .G1(bcd99_2_g1), .E1(bcd99_2_e1), .D1(bcd99_2_d1),
    .C1(bcd99_2_c1), .B2(bcd99_2_b2), .A2(bcd99_2_a2), .F2(bcd99_2_f2), .G2(bcd99_2_g2), .E2(bcd99_2_e2),
    .D2(bcd99_2_d2), .C2(bcd99_2_c2));
  _7_Segment_Display u_7_segment_display_3 (
    .g(bcd99_2_g1), .f(bcd99_2_f1), .a(bcd99_2_a1), .b(bcd99_2_b1), .e(bcd99_2_e1), .d(bcd99_2_d1),
    .c(bcd99_2_c1));  // open: dp
  and and_1 (and_1_out, even_parity_2_out, shift_register_2_p12);
  LED led_5 (.in(and_1_out));
  _7_Segment_Display u_7_segment_display_4 (
    .g(bcd99_2_g2), .f(bcd99_2_f2), .a(bcd99_2_a2), .b(bcd99_2_b2), .e(bcd99_2_e2), .d(bcd99_2_d2),
    .c(bcd99_2_c2));  // open: dp
endmodule

module RL8M (
);

  wire bcd99_1_a1, bcd99_1_a2, bcd99_1_b1, bcd99_1_b2, bcd99_1_c1, bcd99_1_c2, bcd99_1_d1, bcd99_1_d2,
       bcd99_1_e1, bcd99_1_e2, bcd99_1_f1, bcd99_1_f2, bcd99_1_g1, bcd99_1_g2, bcd99_2_a1, bcd99_2_a2,
       bcd99_2_b1, bcd99_2_b2, bcd99_2_c1, bcd99_2_c2, bcd99_2_d1, bcd99_2_d2, bcd99_2_e1, bcd99_2_e2,
       bcd99_2_f1, bcd99_2_f2, bcd99_2_g1, bcd99_2_g2, CANAL, CLOCK, PARIDADE, shift_register_1_p1,
       shift_register_1_p2, shift_register_1_p3, shift_register_1_p4, shift_register_1_p14;
  wire [7:0] buffer_1_out, dipswitch_1_p1, dipswitch_2_p1;

  // DipSwitch dipswitch_1: pin names not known; wires that end beside it: dipswitch_1_p1[0], dipswitch_1_p1[1], dipswitch_1_p1[2], dipswitch_1_p1[3], dipswitch_1_p1[4], dipswitch_1_p1[5], dipswitch_1_p1[6], dipswitch_1_p1[7]
  // DipSwitch dipswitch_2: pin names not known; wires that end beside it: dipswitch_2_p1[0], dipswitch_2_p1[1], dipswitch_2_p1[2], dipswitch_2_p1[3], dipswitch_2_p1[4], dipswitch_2_p1[5], dipswitch_2_p1[6], dipswitch_2_p1[7]
  // NOT_Gate not_1 has open pins: in=CANAL, out=open
  assign buffer_1_out = dipswitch_2_p1;  // Buffer buffer_1, 8 bits wide
  assign buffer_1_out = dipswitch_1_p1;  // Buffer buffer_2, 8 bits wide
  xnor even_parity_1 (PARIDADE, dipswitch_2_p1[0], dipswitch_2_p1[1], dipswitch_2_p1[2], dipswitch_2_p1[3], dipswitch_2_p1[4], dipswitch_2_p1[5], dipswitch_2_p1[6], dipswitch_2_p1[7]);
  xnor even_parity_2 (PARIDADE, dipswitch_1_p1[0], dipswitch_1_p1[1], dipswitch_1_p1[2], dipswitch_1_p1[3], dipswitch_1_p1[4], dipswitch_1_p1[5], dipswitch_1_p1[6], dipswitch_1_p1[7]);
  LED led_1 (.in(PARIDADE));
  LED led_2 (.in(PARIDADE));
  BCD99 bcd99_1 (
    .A(dipswitch_2_p1[0]), .B(dipswitch_2_p1[1]), .C(dipswitch_2_p1[2]), .D(dipswitch_2_p1[3]),
    .E(dipswitch_2_p1[4]), .F(dipswitch_2_p1[5]), .G(dipswitch_2_p1[6]), .H(dipswitch_2_p1[7]),
    .B1(bcd99_1_b1), .A1(bcd99_1_a1), .F1(bcd99_1_f1), .G1(bcd99_1_g1), .E1(bcd99_1_e1), .D1(bcd99_1_d1),
    .C1(bcd99_1_c1), .B2(bcd99_1_b2), .A2(bcd99_1_a2), .F2(bcd99_1_f2), .G2(bcd99_1_g2), .E2(bcd99_1_e2),
    .D2(bcd99_1_d2), .C2(bcd99_1_c2));
  BCD99 bcd99_2 (
    .A(dipswitch_1_p1[0]), .B(dipswitch_1_p1[1]), .C(dipswitch_1_p1[2]), .D(dipswitch_1_p1[3]),
    .E(dipswitch_1_p1[4]), .F(dipswitch_1_p1[5]), .G(dipswitch_1_p1[6]), .H(dipswitch_1_p1[7]),
    .B1(bcd99_2_b1), .A1(bcd99_2_a1), .F1(bcd99_2_f1), .G1(bcd99_2_g1), .E1(bcd99_2_e1), .D1(bcd99_2_d1),
    .C1(bcd99_2_c1), .B2(bcd99_2_b2), .A2(bcd99_2_a2), .F2(bcd99_2_f2), .G2(bcd99_2_g2), .E2(bcd99_2_e2),
    .D2(bcd99_2_d2), .C2(bcd99_2_c2));
  _7_Segment_Display u_7_segment_display_1 (
    .g(bcd99_1_g1), .f(bcd99_1_f1), .a(bcd99_1_a1), .b(bcd99_1_b1), .e(bcd99_1_e1), .d(bcd99_1_d1),
    .c(bcd99_1_c1));  // open: dp
  _7_Segment_Display u_7_segment_display_2 (
    .g(bcd99_2_g1), .f(bcd99_2_f1), .a(bcd99_2_a1), .e(bcd99_2_e1), .d(bcd99_2_d1), .c(bcd99_2_c1));  // open: b, dp
  _7_Segment_Display u_7_segment_display_3 (
    .g(bcd99_2_g2), .f(bcd99_2_f2), .a(bcd99_2_a2), .b(bcd99_2_b2), .e(bcd99_2_e2), .d(bcd99_2_d2),
    .c(bcd99_2_c2));  // open: dp
  _7_Segment_Display u_7_segment_display_4 (
    .g(bcd99_1_g2), .f(bcd99_1_f2), .a(bcd99_1_a2), .b(bcd99_1_b2), .e(bcd99_1_e2), .d(bcd99_1_d2),
    .c(bcd99_1_c2));  // open: dp
  // Shift_Register #(.length(9)) shift_register_1: pin names not known; wires that end beside it: shift_register_1_p1, shift_register_1_p2, shift_register_1_p3, shift_register_1_p4, buffer_1_out[0], buffer_1_out[1], buffer_1_out[2], buffer_1_out[3], buffer_1_out[4], buffer_1_out[5], buffer_1_out[6], buffer_1_out[7], PARIDADE, shift_register_1_p14
  not not_2 (shift_register_1_p3, shift_register_1_p2);
  // OR_Gate or_1 has open pins: out=shift_register_1_p4
  LED led_3 (.in(shift_register_1_p14));
  // Shift_Register #(.length(9)) shift_register_2: pin names not known; wires that end beside it: shift_register_1_p1, CLOCK, shift_register_1_p14
endmodule

// VHDL entity bcd_7seg, as the project stores it:
LIBRARY ieee;
USE ieee.std_logic_1164.all;
ENTITY bcd_7seg IS
PORT (
A,B,C,D : IN STD_LOGIC;
sb,sa,sf,sg,se,sd,sc : OUT STD_LOGIC
);
END bcd_7seg;
ARCHITECTURE trans OF bcd_7seg IS
BEGIN
PROCESS (A,B,C,D)
variable entra: std_logic_vector(3 downto 0);
variable sai : STD_LOGIC_VECTOR(6 DOWNTO 0);
BEGIN
entra := (A,B,C,D);
CASE entra IS
WHEN "0000" =>
sai := NOT("1111110");
WHEN "0001" =>
sai := NOT("0110000");
WHEN "0010" =>
sai := NOT("1101101");
WHEN "0011" =>
sai := NOT("1111001");
WHEN "0100" =>
sai := NOT("0110011");
WHEN "0101" =>
sai := NOT("1011011");
WHEN "0110" =>
sai := NOT("1011111");
WHEN "0111" =>
sai := NOT("1110000");
WHEN "1000" =>
sai := NOT("1111111");
WHEN "1001" =>
sai := NOT("1111011");
WHEN "1010" =>
sai := NOT("1110111");--A
WHEN "1011" =>
sai := NOT("0011111");--b
WHEN "1100" =>
sai := NOT("1001110");--C
WHEN "1101" =>
sai := NOT("0111101");--d
WHEN "1110" =>
sai := NOT("1001111");--E
WHEN "1111" =>
sai := NOT("1000111");--F
WHEN OTHERS =>
sai := NOT("0000000");
END CASE;
sa<=sai(6);
sb<=sai(5);
sc<=sai(4);
sd<=sai(3);
se<=sai(2);
sf<=sai(1);
sg<=sai(0);
END PROCESS;
END;
