// Logisim project cu.circ as structural Verilog: 1 circuit, main circuit main
module main (
  input  RST,
  input  COUNT
);

  wire and_1_out, counter_1_carry, n7447_1_pin3, n7447_1_pin9, n7447_1_pin10, n7447_1_pin11, n7447_1_pin12,
       n7447_1_pin13, n7447_1_pin14, n7447_1_pin15, not_1_out, Tunel;
  wire [3:0] counter_1_q;

  Clock CLK (.out(Tunel));
  not not_1 (not_1_out, RST);
  and and_1 (and_1_out, Tunel, COUNT);
  LED LED_1 (.in(Tunel));
  Counter #(.max('h9), .width(4)) counter_1 (
    .clr(not_1_out), .load(1'b0), .up(1'b1), .count(1'b1), .clk(and_1_out), .carry(counter_1_carry),
    .Q(counter_1_q));  // open: D
  _7447 u_7447_1 (
    .pin1(counter_1_q[1]), .pin2(counter_1_q[2]), .pin3(n7447_1_pin3), .pin4(n7447_1_pin3),
    .pin5(n7447_1_pin3), .pin6(counter_1_q[3]), .pin7(counter_1_q[0]), .pin15(n7447_1_pin15),
    .pin14(n7447_1_pin14), .pin13(n7447_1_pin13), .pin12(n7447_1_pin12), .pin11(n7447_1_pin11),
    .pin10(n7447_1_pin10), .pin9(n7447_1_pin9));
  _7_Segment_Display #(.active("false")) L_7_Segment_Display_1 (
    .g(n7447_1_pin14), .f(n7447_1_pin15), .a(n7447_1_pin13), .b(n7447_1_pin12), .e(n7447_1_pin9),
    .d(n7447_1_pin10), .c(n7447_1_pin11), .dp(Tunel));
  // also tied to VCC on the sheet: n7447_1_pin3
endmodule
