// Logisim project professoruim.circ as structural Verilog
module main (
  input  RESET
);

  wire clock_1_out, count4_1_carr, count4_2_carr, count4_3_carr;
  wire [3:0] count4_1_q, count4_2_q, count4_3_q, count4_4_q;
  wire [6:0] S1, S2, S3, S4;

  Clock clock_1 (.out(clock_1_out));
  _7_Segment_Display L_7_Segment_Display_3 (
    .g(S1[0]), .f(S1[1]), .a(S1[6]), .b(S1[5]), .e(S1[2]), .d(S1[3]), .c(S1[4]), .dp(1'b1));
  LED PISCA (.in(clock_1_out));
  _7_Segment_Display L_7_Segment_Display_4 (
    .g(S2[0]), .f(S2[1]), .a(S2[6]), .b(S2[5]), .e(S2[2]), .d(S2[3]), .c(S2[4]), .dp(1'b1));
  count4 count4_1 (.clk(clock_1_out), .rst(RESET), .q(count4_1_q), .carr(count4_1_carr));
  count4 count4_2 (.clk(count4_1_carr), .rst(RESET), .q(count4_2_q), .carr(count4_2_carr));
  count4 count4_3 (.clk(count4_2_carr), .rst(RESET), .q(count4_3_q), .carr(count4_3_carr));
  count4 count4_4 (.clk(count4_3_carr), .rst(RESET), .q(count4_4_q));  // open: carr
  _7_Segment_Display L_7_Segment_Display_2 (
    .g(S3[0]), .f(S3[1]), .a(S3[6]), .b(S3[5]), .e(S3[2]), .d(S3[3]), .c(S3[4]), .dp(1'b1));
  bcd_7seg bcd_7seg_1 (.entra(count4_1_q), .sai(S1));
  bcd_7seg bcd_7seg_2 (.entra(count4_2_q), .sai(S2));
  bcd_7seg bcd_7seg_3 (.entra(count4_3_q), .sai(S3));
  bcd_7seg bcd_7seg_4 (.entra(count4_4_q), .sai(S4));
  _7_Segment_Display L_7_Segment_Display_1 (
    .g(S4[0]), .f(S4[1]), .a(S4[6]), .b(S4[5]), .e(S4[2]), .d(S4[3]), .c(S4[4]), .dp(1'b1));
endmodule

// VHDL entity count4, as the project stores it:
--------------------------------------------------------------------------------
-- Project :
-- File    :
-- Autor   :
-- Date    :
--
--------------------------------------------------------------------------------
-- Description :
--
--------------------------------------------------------------------------------

LIBRARY ieee;
USE ieee.std_logic_1164.all;
USE ieee.std_logic_unsigned.all;
ENTITY count4 IS
PORT (
clk : IN STD_LOGIC;
rst : IN STD_LOGIC;
q : OUT STD_LOGIC_VECTOR(3 DOWNTO 0);
carr : OUT STD_LOGIC
);
END ENTITY count4;
ARCHITECTURE trans OF count4 IS
SIGNAL count : STD_LOGIC_VECTOR(3 DOWNTO 0);
BEGIN

PROCESS (clk, rst)
BEGIN
IF (rst = '1') THEN
count <= "0000";
ELSE
IF (clk'EVENT AND clk = '1') THEN
IF (count ="1001") THEN
carr<='1';
ELSE
carr<='0';
END IF;
IF (count >= "1001") THEN
count <= "0000";
ELSE
count <= count + "0001";
END IF;
END IF;
END IF;
END PROCESS;
q <= count;
END ARCHITECTURE trans;

// VHDL entity bcd_7seg, as the project stores it:
--------------------------------------------------------------------------------
-- Project :
-- File    :
-- Autor   :
-- Date    :
--
--------------------------------------------------------------------------------
-- Description :
--
--------------------------------------------------------------------------------

LIBRARY ieee;
USE ieee.std_logic_1164.all;
ENTITY bcd_7seg IS
PORT (
entra : IN STD_LOGIC_VECTOR(3 DOWNTO 0);
sai : OUT STD_LOGIC_VECTOR(6 DownTO 0)
);
END bcd_7seg;
ARCHITECTURE trans OF bcd_7seg IS
BEGIN
PROCESS (entra)
BEGIN
CASE entra IS
WHEN "0000" =>
sai <= NOT("1111110");
WHEN "0001" =>
sai <= NOT("0110000");
WHEN "0010" =>
sai <= NOT("1101101");
WHEN "0011" =>
sai <= NOT("1111001");
WHEN "0100" =>
sai <= NOT("0110011");
WHEN "0101" =>
sai <= NOT("1011011");
WHEN "0110" =>
sai <= NOT("1011111");
WHEN "0111" =>
sai <= NOT("1110000");
WHEN "1000" =>
sai <= NOT("1111111");
WHEN "1001" =>
sai <= NOT("1111011");
WHEN OTHERS =>
sai <= NOT("0000000");
END CASE;
END PROCESS;

END trans;
